# Fritzing sketch CarControl (saved by Fritzing 0.9.3b)
breadboards: 1

parts:
  hc-sr1 = hc-sr04
  Part1 = Arduino Uno (Rev3)
  R3 = Resistor [tolerance=±5% resistance=10k package=THT]
  R1 = Resistor [tolerance=±5% resistance=10k package=THT]
  R2 = Resistor [tolerance=±5% resistance=10k package=THT]
  Part2 = Bluetooth HC-05 Macho

nets:
  VCC: hc-sr1.VCC, Part1.5V, Part2.VCC
  N1: hc-sr1.Trig, Part1.D12/MISO
  N2: hc-sr1.Echo, Part1.D11_PWM/MOSI
  GND: hc-sr1.GND, Part1.GND, R2.Pin_0, Part2.GND
  N3: Part1.D8, R3.Pin_0, R1.Pin_0
  N4: Part1.D7, Part2.TXD
  N5: R3.Pin_1, R2.Pin_1
  N6: R1.Pin_1, Part2.RXD
