# Fritzing sketch CarControl (saved by Fritzing 0.9.3b)
breadboards: 1

parts:
  hc-sr04 = hc-sr04
  Part1 = Arduino Uno (Rev3)
  R3 = Resistor [tolerance=±5% resistance=10k package=THT]
  R1 = Resistor [tolerance=±5% resistance=10k package=THT]
  R2 = Resistor [tolerance=±5% resistance=10k package=THT]
  HC-05 = Bluetooth HC-05 [part_number=ZS-040]

nets:
  VCC: hc-sr04.VCC, Part1.5V, HC-05.VCC
  N1: hc-sr04.Trig, Part1.D12/MISO
  N2: hc-sr04.Echo, Part1.D11_PWM/MOSI
  GND: hc-sr04.GND, Part1.GND, R2.Pin_0, HC-05.GND
  N3: Part1.D8, R3.Pin_0, R1.Pin_0
  N4: Part1.D7, HC-05.TXD
  N5: R3.Pin_1, R2.Pin_1
  N6: R1.Pin_1, HC-05.RXD

custom parts:
  Bluetooth HC-05: Amended and modified From Computação na Escola
